# Fritzing sketch remote_schematic (saved by Fritzing 0.9.3b)

parts:
  Bauteil1 = Arduino Mega ADK (Rev3)
  Bauteil2 = Bluetooth HC-05 Macho
  Joystick = Thumb Joystick
  part = Resistor [tolerance=±5% resistance=1k package="2010 [SMD]"]
  part_2 = Resistor [tolerance=±5% resistance=2k package="2010 [SMD]"]

nets:
  N1: Bauteil1.A0, Joystick.VERT
  N2: Bauteil1.A1, Joystick.HORZ
  N3: Bauteil1.D18/TX1, Bauteil2.TXD
  N4: Bauteil1.D17/RX2, part.Pin_0
  5V: Bauteil1.5V, Joystick.VCC
  GND: Bauteil1.GND, Joystick.GND
  N5: Bauteil2.RXD, part_2.Pin_1
